// Logisim project lock.circ as structural Verilog: 7 circuits, main circuit Lock
module Lock (
  output Message,
  output Lock_State
);

  wire A_out, B_out, Button_Controller_2_press_output, Button_Controller_press_output,
       Button_Logic_button_output, Button_Logic_enable, Clock_out;

  Clock Clock (.out(Clock_out));
  Button A (.out(A_out));
  Button B (.out(B_out));
  Button_Controller Button_Controller (
    .Button_Input(A_out), .Clock(Clock_out), .Press_Output(Button_Controller_press_output));
  Button_Controller Button_Controller_2 (
    .Button_Input(B_out), .Clock(Clock_out), .Press_Output(Button_Controller_2_press_output));
  Button_Logic Button_Logic (
    .A_Button_Input(Button_Controller_press_output), .B_Button_Input(Button_Controller_2_press_output),
    .Button_Output(Button_Logic_button_output), .Enable(Button_Logic_enable));
  Lock_Controller Lock_Controller (
    .Button_Input(Button_Logic_button_output), .Clock(Clock_out), .Enable(Button_Logic_enable),
    .Message(Message), .Lock_State(Lock_State));
endmodule

module Lock_Controller (
  input  Button_Input,
  input  Clock,
  input  Enable,
  output Message,
  output Lock_State
);

  wire _3_Bit_State_Register_p0, _3_Bit_State_Register_p1, _3_Bit_State_Register_p2, Lock_Logic_n0,
       Lock_Logic_n1, Lock_Logic_n2;

  Lock_Logic Lock_Logic (
    .in_1(Button_Input), .p2(_3_Bit_State_Register_p2), .p1(_3_Bit_State_Register_p1),
    .p0(_3_Bit_State_Register_p0), .out_5(Message), .out_6(Lock_State), .n2(Lock_Logic_n2),
    .n1(Lock_Logic_n1), .n0(Lock_Logic_n0));
  State_Register _3_Bit_State_Register (
    .Clock(Clock), .Enable(Enable), .n2(Lock_Logic_n2), .n1(Lock_Logic_n1), .n0(Lock_Logic_n0),
    .p2(_3_Bit_State_Register_p2), .p1(_3_Bit_State_Register_p1), .p0(_3_Bit_State_Register_p0));
endmodule

module Lock_Logic (
  input  in_1,
  input  p2,
  input  p1,
  input  p0,
  output out_5,
  output out_6,
  output n2,
  output n1,
  output n0
);


  assign n0 = in_1;
  assign n1 = in_1;
  assign n2 = in_1;
  assign out_5 = in_1;
  assign out_6 = in_1;
  assign p0 = in_1;
  assign p1 = in_1;
  assign p2 = in_1;
endmodule

module State_Register (
  input  Clock,
  input  Enable,
  input  n2,
  input  n1,
  input  n0,
  output p2,
  output p1,
  output p0
);

  D_Flip_Flop d_ff_1 (.clk(Clock), .D(n2), .Q(p2), .en(Enable));  // open: Qn, preset, reset
  D_Flip_Flop d_ff_2 (.clk(Clock), .D(n1), .Q(p1), .en(Enable));  // open: Qn, preset, reset
  D_Flip_Flop d_ff_3 (.clk(Clock), .D(n0), .Q(p0), .en(Enable));  // open: Qn, preset, reset
endmodule

module Button_Controller (
  input  Button_Input,
  input  Clock,
  output Press_Output
);

  wire button_controller_logic_1_next_state, d_ff_1_q;

  Button_Controller_Logic button_controller_logic_1 (
    .Activation_Input(Button_Input), .Current_State(d_ff_1_q), .Button_Press_Output(Press_Output),
    .Next_State(button_controller_logic_1_next_state));
  D_Flip_Flop d_ff_1 (
    .clk(Clock), .D(button_controller_logic_1_next_state), .Q(d_ff_1_q));  // open: Qn, preset, en, reset
endmodule

module Button_Logic (
  input  A_Button_Input,
  input  B_Button_Input,
  output Button_Output,
  output Enable
);

  wire not_1_out;

  not not_1 (not_1_out, A_Button_Input);
  and and_1 (Button_Output, not_1_out, B_Button_Input);
  xor xor_1 (Enable, B_Button_Input, A_Button_Input);
endmodule

module Button_Controller_Logic (
  input  Activation_Input,
  input  Current_State,
  output Button_Press_Output,
  output Next_State
);

  wire not_1_out;

  not not_1 (not_1_out, Activation_Input);
  and and_1 (Button_Press_Output, not_1_out, Current_State);

  assign Next_State = Activation_Input;
endmodule
